# Fritzing sketch FritzElétrico (saved by Fritzing 0.9.3b)
breadboards: 2

parts:
  U1 = ESP8266 NodeMCU LoLin module
  M2 = DC Motor
  U2 = 74HC595 [package="DIP16 [THT]"]
  LED2 = LED - 5mm [color="Red (633nm)" package="5 mm [THT]"]
  LED3 = LED - 5mm [color="Red (633nm)" package="5 mm [THT]"]
  LED4 = LED - 5mm [color="Red (633nm)" package="5 mm [THT]"]
  LED5 = LED - 5mm [color="Red (633nm)" package="5 mm [THT]"]
  LED6 = LED - 5mm [color="Red (633nm)" package="5 mm [THT]"]
  LED7 = LED - 5mm [color="Red (633nm)" package="5 mm [THT]"]
  LED8 = LED - 5mm [color="Red (633nm)" package="5 mm [THT]"]
  LED9 = LED - 5mm [color="Red (633nm)" package="5 mm [THT]"]
  R2 = Resistor [tolerance=±5% resistance=220 package="1206 [SMD]"]
  R3 = Resistor [tolerance=±5% resistance=220 package="1206 [SMD]"]
  R4 = Resistor [tolerance=±5% resistance=220 package="1206 [SMD]"]
  R5 = Resistor [tolerance=±5% resistance=220 package="1206 [SMD]"]
  R6 = Resistor [tolerance=±5% resistance=220 package="1206 [SMD]"]
  R7 = Resistor [tolerance=±5% resistance=220 package="1206 [SMD]"]
  R8 = Resistor [tolerance=±5% resistance=220 package="1206 [SMD]"]
  R9 = Resistor [tolerance=±5% resistance=220 package="1206 [SMD]"]
  DFRobot_DFPlayer_Mini1 = DFRobot DFPlayer Mini [part_number=DFR0299]
  SP1 = SPEAKER [package=pcb_mount_speaker]
  R11 = Resistor [tolerance=±5% resistance=220 package="1206 [SMD]"]
  VCC1 = Battery block 9V
  R12 = Resistor [tolerance=±5% resistance=220 package="1206 [SMD]"]
  M1 = DC Motor
  R13 = Resistor [tolerance=±5% resistance=220 package="1206 [SMD]"]

nets (from the breadboard view):
  N1: U1.D1, M2.pin_1
  N2: U1.D2, M1.pin_1
  N3: U1.D3, M2.pin_2
  N4: U1.D4, M1.pin_2
  N5: U1.3V3, U2.MR
  N6: U1.GND, U2.OE, VCC1.-
  N7: U1.D5, U2.SH_CP
  N8: U1.D6, U2.ST_CP
  N9: U1.D7, DFRobot_DFPlayer_Mini1.BUSY
  N10: U1.D8, U2.DS
  N11: U1.RX, R11.Pin_0
  N12: U1.TX, DFRobot_DFPlayer_Mini1.TX
  N13: U2.Q1, R3.Pin_1
  N14: U2.Q2, R4.Pin_1
  N15: U2.Q3, R5.Pin_1
  N16: U2.Q4, R6.Pin_1
  N17: U2.Q5, R7.Pin_1
  N18: U2.Q6, R8.Pin_1
  N19: U2.Q7, R9.Pin_1
  N20: U2.Q0, R2.Pin_1
  N21: U2.VCC, VCC1.+, R12.Pin_1, R13.Pin_0
  N22: LED2.cathode, LED3.cathode, LED4.cathode, LED5.cathode, LED6.cathode, LED7.cathode, LED8.cathode, LED9.cathode
  N23: LED2.anode, R2.Pin_0
  N24: LED3.anode, R3.Pin_0
  N25: LED4.anode, R4.Pin_0
  N26: LED5.anode, R5.Pin_0
  N27: LED6.anode, R6.Pin_0
  N28: LED7.anode, R7.Pin_0
  N29: LED8.anode, R8.Pin_0
  N30: LED9.anode, R9.Pin_0
  N31: DFRobot_DFPlayer_Mini1.VCC, R13.Pin_1
  N32: DFRobot_DFPlayer_Mini1.RX, R11.Pin_1
  N33: DFRobot_DFPlayer_Mini1.SPK_1, SP1.+
  N34: DFRobot_DFPlayer_Mini1.GND-1, DFRobot_DFPlayer_Mini1.GND-2
  N35: DFRobot_DFPlayer_Mini1.SPK_2, SP1.-

custom parts:
  ESP8266 NodeMCU LoLin module: ESP8266 based NodeMCU
